# Fritzing sketch DoorOpener (saved by Fritzing 0.7.6b)
breadboards: 1

parts:
  Arduino_Ethernet_Shield1 = Arduino Ethernet Shield
  R1 = Resistor [tolerance=±5% resistance=220 package=THT]
  R2 = Resistor [tolerance=±5% resistance=220 package=THT]
  U1 = Optocoupler [package=THT]
  LED1 = LED - 3mm [color="Red (633nm)" package="3 mm [THT]"]

nets:
  N1: Arduino_Ethernet_Shield1.D8, R1.Pin_0
  N2: Arduino_Ethernet_Shield1.GND, LED1.anode
  N3: R1.Pin_1, R2.Pin_0
  N4: R2.Pin_1, U1.Pin_1
  N5: U1.Pin_2, LED1.cathode

notes:
  connect door opener
